# Fritzing sketch WeMosD1 (saved by Fritzing 0.9.4)
breadboards: 1

parts:
  WeMos_D1_Mini1 = WeMos D1 Mini
  LED1 = RGB LED (com. cathode, rbg) [package="5 mm [THT]"]
  S1_-_Black = Pushbutton [package=THT]
  R1 = Resistor [tolerance=±1% resistance=470 package="2512 [SMD]"]
  R2 = Resistor [tolerance=±1% resistance=2k package="2512 [SMD]"]
  R3 = Resistor [tolerance=±1% resistance=5.1k package="2512 [SMD]"]
  S2_-_Yellow = Pushbutton [package=THT]
  S3_-_Green = Pushbutton [package=THT]
  S4_-_Red = Pushbutton [package=THT]

nets:
  N1: WeMos_D1_Mini1.D2, R1.Pin_0
  N2: WeMos_D1_Mini1.D3, R2.Pin_0
  N3: WeMos_D1_Mini1.D4, R3.Pin_0
  N4: WeMos_D1_Mini1.D5, S1_-_Black.leg1
  N5: WeMos_D1_Mini1.D6, S2_-_Yellow.leg1
  N6: WeMos_D1_Mini1.D7, S3_-_Green.leg1
  N7: WeMos_D1_Mini1.D8, S4_-_Red.leg1
  N8: WeMos_D1_Mini1.G, LED1.common_cathode, S1_-_Black.leg0, S2_-_Yellow.leg0, S3_-_Green.leg0, S4_-_Red.leg0
  N9: LED1.red_anode, R1.Pin_1
  N10: LED1.blue_anode, R2.Pin_1
  N11: LED1.green_anode, R3.Pin_1
