# Fritzing sketch temp_sensor (saved by Fritzing 0.9.4)
breadboards: 1

parts:
  WeMos_D1_Mini1 = WeMos D1 Mini
  LED1 = RGB LED (com. cathode, rbg) [package="5 mm [THT]"]
  R1 = Resistor [tolerance=±1% resistance=470 package="2512 [SMD]"]
  R2 = Resistor [tolerance=±1% resistance=2k package="2512 [SMD]"]
  R3 = Resistor [tolerance=±1% resistance=5.1k package="2512 [SMD]"]
  DS1 = DS18B20 1-Wire Temperature Sensor [part_number=DS18B20]
  R4 = Resistor [tolerance=±5% resistance=4.7k package=THT]

nets:
  3V3: WeMos_D1_Mini1.3V3, DS1.VDD, R4.Pin_1
  N1: WeMos_D1_Mini1.D1, DS1.DQ, R4.Pin_0
  N2: WeMos_D1_Mini1.D2, R1.Pin_1
  N3: WeMos_D1_Mini1.D3, R3.Pin_1
  N4: WeMos_D1_Mini1.D4, R2.Pin_1
  N5: WeMos_D1_Mini1.G, LED1.common_cathode, DS1.GND
  N6: LED1.red_anode, R1.Pin_0
  N7: LED1.blue_anode, R2.Pin_0
  N8: LED1.green_anode, R3.Pin_0
